# Fritzing sketch Dado Elettronico (saved by Fritzing 0.9.3b)
breadboards: 2

parts:
  Componente1 = Arduino Uno (Rev3)
  R1 = Resistor [tolerance=±5% resistance=220 package=THT]
  R2 = Resistor [tolerance=±5% resistance=220 package=THT]
  R3 = Resistor [tolerance=±5% resistance=220 package=THT]
  R4 = Resistor [tolerance=±5% resistance=220 package=THT]
  7_Segment1 = 7 Segment Display
  R5 = Resistor [tolerance=±5% resistance=220 package=THT]  # not connected
  R6 = Resistor [tolerance=±5% resistance=220 package=THT]
  R7 = Resistor [tolerance=±5% resistance=220 package=THT]
  R8 = Resistor [tolerance=±5% resistance=220 package=THT]
  U1 = 74HC595 [package="DIP16 [THT]"]
  S1 = Pushbutton [package="[THT]"]
  R9 = Resistor [tolerance=±5% resistance=220 package=THT]

nets:
  N1: Componente1.D2, S1.Pin_3, S1.Pin_4, R9.Pin_1
  5V: Componente1.5V, U1.MR, U1.VCC, R9.Pin_0
  N2: Componente1.GND, R2.Pin_0, U1.Q5, U1.OE, S1.Pin_1, S1.Pin_2
  N3: R1.Pin_1, 7_Segment1.Segment_G, 7_Segment1.Segment_F
  N4: R3.Pin_1, R8.Pin_1, U1.Q1
  N5: R4.Pin_0, 7_Segment1.Segment_B, 7_Segment1.Segment_A
  N6: R4.Pin_1, U1.Q0
  N7: 7_Segment1.Segment_D, R6.Pin_1
  N8: 7_Segment1.Segment_DP, R7.Pin_0
